# Fritzing sketch garage (saved by Fritzing 0.9.3b)
circuit board: 8.46667cm x 5.64444cm
breadboards: 2

parts:
  Part1 = Arduino Nano (Rev3.0)
  hc-sr1 = hc-sr04
  LED1 = LED - 3mm [color="Red (633nm)" package="3 mm [THT]"]
  LED3 = LED - 3mm [color="Green (565nm)" package="3 mm [THT]"]
  LED2 = LED - 3mm [color="Yellow (595nm)" package="3 mm [THT]"]
  MCU1 = Raspberry Pi Zero
  hc-sr2 = hc-sr04
  R6 = Resistor [tolerance=±5% resistance=330 package="2512 [SMD]"]
  R7 = Resistor [tolerance=±5% resistance=470 package="2512 [SMD]"]
  U1 = Sharp PC817 [package=THT]
  R8 = Resistor [tolerance=±5% resistance=330 package=THT]
  U2 = Sharp PC817 [package=THT]

nets:
  N1: Part1.D2, hc-sr1.Echo
  N2: Part1.D3, hc-sr1.Trig
  N3: Part1.D4, LED3.anode
  N4: Part1.D5, LED2.anode
  N5: Part1.D6, Part1.D7, LED1.anode
  VIN: Part1.VIN, hc-sr1.VCC, U2.Pin_4
  GND: Part1.GND, Part1.RESET, hc-sr1.GND, MCU1.pin_6, MCU1.pin_30, MCU1.pin_34, MCU1.pin_39, hc-sr2.GND, R7.Pin_1, U1.Pin_2, R8.Pin_1, U2.Pin_1
  N6: LED1.cathode, LED3.cathode, LED2.cathode, R8.Pin_0
  N7: MCU1.pin_2, MCU1.pin_4, hc-sr2.VCC, U2.Pin_3
  N8: MCU1.pin_3, U2.Pin_2
  N9: MCU1.pin_8, U1.Pin_1
  N10: MCU1.pin_10, R7.Pin_0
  N11: MCU1.pin_12, hc-sr2.Trig
  N12: hc-sr2.Echo, R6.Pin_1

notes:
  Abstandswarner
  Garagentorkontrolle

// code stored in the sketch: Untitled.ino

